// Logisim project Implementation of NOT, AND, OR, XOR and XNOR using NOR gates.circ as structural Verilog: 1 circuit, main circuit main
module main (
  input  A,
  input  in_2,
  input  A_2,
  input  A_3,
  input  A_4,
  input  B,
  input  B_2,
  input  B_3,
  input  A_5,
  input  B_4,
  input  A_6,
  input  B_5,
  input  A_7,
  input  B_6,
  output A_A__prime,
  output A_prime_B_prime__prime___AB,
  output AB,
  output A_B,
  output A_B_2,
  output A_prime,
  output F___XNOR,
  output F___XOR
);

  wire nor_2_out, nor_3_out, nor_4_out, nor_5_out, nor_6_out, nor_7_out, nor_10_out, nor_11_out, nor_12_out,
       nor_13_out;

  nor nor_1 (A_A__prime, A, A);
  not not_1 (A_prime, A_5);
  nor nor_2 (nor_2_out, A_6, B_5);
  nor nor_3 (nor_3_out, A_6, nor_2_out);
  nor nor_4 (nor_4_out, nor_2_out, B_5);
  nor nor_5 (nor_5_out, in_2, in_2);
  nor nor_6 (nor_6_out, B_4, B_4);
  nor nor_7 (nor_7_out, nor_3_out, nor_4_out);
  nor nor_8 (A_prime_B_prime__prime___AB, nor_5_out, nor_6_out);
  nor nor_9 (F___XOR, nor_7_out, nor_7_out);
  and and_1 (AB, A_2, B);
  nor nor_10 (nor_10_out, A_3, B_2);
  nor nor_11 (nor_11_out, A_7, B_6);
  nor nor_12 (nor_12_out, A_7, nor_11_out);
  nor nor_13 (nor_13_out, nor_11_out, B_6);
  nor nor_14 (A_B, nor_10_out, nor_10_out);
  or or_1 (A_B_2, A_4, B_3);
  nor nor_15 (F___XNOR, nor_12_out, nor_13_out);

  // Notes on the sheet:
  //   NOT GATE
  //   A'
  //   (A+B)'
  //   (A+(A+B)')'
  //   (B+(A+B)')'
  //   F: Experimental Data
  //   A'
  //   B'
  //   XOR
  //   XNOR
  //   AND GATE
  //   Figure F2: Implementation of NOT, AND, OR, XOR and XNOR using NOR gates
  //   (A+B)'
  //   (A+B)'
  //   XNOR
  //   OR GATE
  //   (A+(A+B)')'
  //   (B+(A+B)')'
  //   A
endmodule
