// Logisim project Implementation of XOR and XNOR using NAND gates.circ as structural Verilog: 1 circuit, main circuit main
module main (
  input  A,
  input  B,
  input  A_2,
  input  B_2,
  output F___XOR,
  output F___XNOR
);

  wire nand_1_out, nand_2_out, nand_3_out, nor_1_out, nor_2_out, nor_3_out;

  nand nand_1 (nand_1_out, A, B);
  nor nor_1 (nor_1_out, A_2, B_2);
  nand nand_2 (nand_2_out, A, nand_1_out);
  nand nand_3 (nand_3_out, nand_1_out, B);
  nor nor_2 (nor_2_out, A_2, nor_1_out);
  nor nor_3 (nor_3_out, nor_1_out, B_2);
  nand nand_4 (F___XOR, nand_2_out, nand_3_out);
  nor nor_4 (F___XNOR, nor_2_out, nor_3_out);

  // Notes on the sheet:
  //   (AB)'
  //   (A+B)'
  //   F: Experimental Data
  //   (A(AB)')'
  //   (B(AB)')'
  //   Figure F1: Implementation of XOR and XNOR using NAND gates
  //   (A+(A+B)')'
  //   (B+(A+B)')'
endmodule
