// Logisim project Logic Diagram for (F = AB'C) Boolean function using only NAND gate.circ as structural Verilog: 1 circuit, main circuit main
module main (
  input  W,
  input  X,
  input  Z,
  output F___WX_prime_Z
);

  wire nand_1_out, nand_2_out, nand_3_out, nand_4_out;

  nand nand_1 (nand_1_out, X, X);
  nand nand_2 (nand_2_out, W, nand_1_out);
  nand nand_3 (nand_3_out, nand_2_out, nand_2_out);
  nand nand_4 (nand_4_out, nand_3_out, Z);
  nand nand_5 (F___WX_prime_Z, nand_4_out, nand_4_out);
endmodule
